# Fritzing sketch stib-iot (saved by Fritzing 0.9.3b)
breadboards: 2

parts:
  U1 = NodeMCU V1.0
  VCC1 = 4 x AAA Battery Mount
  S1 = Momentary Switch [package=ksa_sealed_tac_switch]
  R1 = Resistor [tolerance=±5% resistance=10k package="1206 [SMD]"]
  R2 = Resistor [tolerance=±5% resistance=10k package="1206 [SMD]"]
  S3 = Toggle Switch [package=THT]
  Composant1 = LCD1602-I2C
  S4 = Momentary Switch [package=ksa_sealed_tac_switch]
  S5 = Momentary Switch [package=ksa_sealed_tac_switch]
  R3 = Resistor [tolerance=±5% resistance=10k package="1206 [SMD]"]

nets:
  N1: U1.D1, Composant1.SCL
  N2: U1.D2, Composant1.SDA
  N3: U1.D4, S1.2
  N4: U1.3V3, S1.4, S4.4, S5.4
  GND: U1.GND, R1.Pin_1, R2.Pin_1, S3.L2, Composant1.GND, R3.Pin_0
  N5: U1.D5, S4.2
  N6: U1.D6, S5.2
  VIN: U1.Vin, VCC1.+, Composant1.VCC
  N7: VCC1.-, S3.L1
  N8: S1.1, R1.Pin_0
  N9: R2.Pin_0, S4.1
  N10: S5.1, R3.Pin_1

custom parts:
  NodeMCU V1.0: ESP9266 based NodeMCU
  LCD1602-I2C: A standard character display, usually with 2x16 characters. Comes in many colors with LCM1602 IIC attached.

// code stored in the sketch: config.h
#pragma once
#include "Favourite.h"

/**WiFi config*/
#define WIFI_SSID "YOUR_SSID"
#define WIFI_PWD  "YOUR_PASSWORD"

/**Stib-Mivb Api Token*/
#define API_TOKEN "Bearer YOUR_BEARER_TOKEN";
/**Refresh rate (in sec) in the passing time screen */
#define REFRESH_RATE_SEC 15

/** Stops ids. Can be found in the GTFS (stops.txt)*/
const Favourite favourites[5] = {
  Favourite("5311", "Tram > Buyl"),
  Favourite("1715", "34 > Auderghem"),
  Favourite("8211", "Metro > Centre"),  
  Favourite("5267", "Tram > Rogier"),
  Favourite("8212", "Metro > Auderg")
};

// code stored in the sketch: Favourite.h
#pragma once

class Favourite{
  public:
    String stopId;
    String label;

    Favourite(String stopId, String label) : 
      stopId(stopId),
      label(label) {
        
      }  

    String getDisplay(){
      return label;
    }
};

// code stored in the sketch: PassingTime.h
#pragma once

class PassingTime{
  String line;
  String destination;
  String expectedTime;
  unsigned long expectedTimeInSec;

  public:
    PassingTime(String line, String destination, String expectedTime) : 
      line(line),
      destination(destination),
      expectedTime(expectedTime)
    {      
      int hour = expectedTime.substring(11, 13).toInt();
      int min = expectedTime.substring(14, 16).toInt();
      int sec = expectedTime.substring(17, 19).toInt();
      expectedTimeInSec = hour*3600 + min*60 + sec;
    }

    String getLine(){
      return line;
    }

    String getDestination(){
      return destination;
    }

    String getRawExpectedTime(){
      return expectedTime;
    }

    /** Calculate the remaining time in min
     *  If difference is less than 45sec, count it as 0, if greater than 45sec, count the full minute
     *  When current time is 21h28m14s and it is expected at 21h30m00s, it should show 2min
     *  When current time is 21h28m16s and it is expected at 21h30m00s, it should show 1min
     *  
     *  When current time is greater than the expected time, return 0 as incoming.
     */
    long getRemainingTime(unsigned long secSinceBeginOfDay){
      long diff = expectedTimeInSec - secSinceBeginOfDay;
      if( diff < -5*60){
        diff = (24*3600 - secSinceBeginOfDay) + expectedTimeInSec;
      } else if( diff < 60){
        return 0;
      }
      if( (diff % 60)>45){
        return (diff/60)+1;
      }else{
        return diff/60;
      }
    }
};


class PassingTimeResponse{
  public:
    int numberOfResponses = 0;
    PassingTime **passingTimes;
  
    PassingTimeResponse(PassingTime **items, int arraySize){
      passingTimes = items;
      numberOfResponses = arraySize;    
    }
};

// code stored in the sketch: PassingTimeService.h
#pragma once
#include "config.h"
#include "PassingTime.h"

//Librairies
#include "ArduinoJson.h"
#include <ArduinoSort.h>
#include <ESP8266HTTPClient.h>
#include <WiFiClientSecureBearSSL.h>

/** STIB-MIVB endpoint configuration */
const String host = "https://opendata-api.stib-mivb.be";
const int httpsPort = 443;
const String endPointToken = "/token";
const String endPointPassingTime = host + "/OperationMonitoring/3.0/PassingTimeByPoint";
// Use web browser to view and copy
// SHA1 fingerprint of the certificate
const char *fingerprint = "5f 88 a4 69 77 f0 69 00 5d 6f 71 19 3d e2 2e 20 44 48 f0 b3";

DynamicJsonBuffer jsonBuffer(512);

bool sortPassingTimes(PassingTime *a, PassingTime *b){
  return a->getRawExpectedTime() > b->getRawExpectedTime();
}

PassingTimeResponse* getPassingTimeResponse(JsonArray& passingTimesArr){
  int i = 0;
  static PassingTime *passingTimes[10];
  for (JsonObject& val : passingTimesArr){
    passingTimes[i] = new PassingTime(val[F("lineId")].as<String>(), val[F("destination")][F("fr")].as<String>(), val[F("expectedArrivalTime")].as<String>());
    i++;
  }
  sortArray(passingTimes, i, sortPassingTimes);
  
  return new PassingTimeResponse(passingTimes, i);
}

PassingTimeResponse* getPassingTime(String stopId){
  String url = endPointPassingTime + "/" + stopId;
  Serial.print(F("[HTTPS] begin: "));
  Serial.println(url);
  
  std::unique_ptr<BearSSL::WiFiClientSecure>client(new BearSSL::WiFiClientSecure);
  client->setFingerprint(fingerprint);
  HTTPClient http;
  if (http.begin(*client, url)) {  // HTTP
      http.addHeader(F("Accept"), F("application/json"));
      http.addHeader(F("Authorization"), API_TOKEN);
      Serial.println(F("[HTTPS] GET..."));
      // start connection and send HTTP header
      int httpCode = http.GET();
      PassingTimeResponse * passingTimeResponse;
      if (httpCode > 0) {
        // HTTP header has been send and Server response header has been handled
        Serial.print(F("[HTTPS] GET... code:"));
        Serial.println(httpCode);
        
        // file found at server
        if (httpCode == HTTP_CODE_OK || httpCode == HTTP_CODE_MOVED_PERMANENTLY) {
          String payload = http.getString();
          JsonObject& root = jsonBuffer.parseObject(payload);
          if(!root.success()){
            Serial.println(F("Fail to parse object"));  
            return 0;
          }
          JsonArray& passingTimesArr = root[F("points")][0][F("passingTimes")];
          if(!passingTimesArr.success()){
            Serial.println(F("Fail to parse passingTimes"));  
            return 0;
          }
          passingTimeResponse = getPassingTimeResponse(passingTimesArr);
        }
      } else {
        Serial.print(F("[HTTPS] GET... failed, error: "));
        Serial.println(http.errorToString(httpCode));
      }

      http.end();
      return passingTimeResponse;
  } else {
    Serial.println(F("[HTTPS] Unable to connect"));
  }
  return 0;
}

// code stored in the sketch: STIB_PassingTime.ino
/*
    Small device to retrieve the passing time of the STIB-MIVB public transport at given stops.
    These stops are hardcoded in the code as favourites. 
    The app consists in 2 screen. 
    - The selection of the line from the favourite list.
    - Displaying the time at station
    The user has 3 push buttons. 
    2 for going up/down. 1 for selecting a favourite/going back to favourites page

    Components:
    - NodeMcu
    - LCD-I2C
    - 3 push buttons
    - 3 10K Ohm resistors

    Librairies:
    - ArduinoJson: https://arduinojson.org/
    - ArduinoSort: https://github.com/emilv/ArduinoSort
    - LiquidCrystal I2C: https://github.com/johnrickman/LiquidCrystal_I2C

    Resources:
    - Configure NodeMcu: https://www.youtube.com/watch?v=p06NNRq5NTU

    TODO:
    - Regenerate token
    - Fix memory leak when making couple of Http calls
    v Get remaining time instead of expected time arrival
    v Format the remaining time to be at the end of the line + use down arrow instead of 0 + align texts
    v Auto refresh every 15sec
    - 3D print case
*/
#define APP_NAME  "Stib IOT - " __FILE__
#define APP_VERSION  "v0.2-" __DATE__ " " __TIME__
#define DEBUG true
#include "PassingTime.h"
#include "PassingTimeService.h"
#include "Favourite.h"
//Configure WIFI_SSID, WIFI_PWD, API_TOKEN, REFRESH_RATE_SEC and favourites
#include "config.h"

/** Librairies */
#include <ESP8266WiFi.h>
#include <Wire.h>  // This library is already built in to the Arduino IDE
#include <LiquidCrystal_I2C.h> //This library you can add via Include Library > Manage Library > 
#include <time.h>

enum UP_DOWN{
  UP,
  DOWN
};

/** Pin Layout 
  * D1: SCL
  * D2: SDA
*/
LiquidCrystal_I2C lcd(0x27, 16, 2);
#define UP_BUTTON D4
#define SELECT_BUTTON D5
#define DOWN_BUTTON D6

uint8_t down_arrow[8]  = {0x4,0x4,0x4,0x4,0xff,0xe,0x4};
const String DOWN_ARROW = String("\1");
void(* resetFunc) (void) = 0; //declare reset function @ address 0

void setup() {
  Serial.begin(115200);
  Serial.println();
  Serial.println(APP_NAME);
  Serial.println(APP_VERSION);
  if(DEBUG)Serial.println(F("Debug mode"));
  
  
  pinMode(UP_BUTTON, INPUT);
  pinMode(SELECT_BUTTON, INPUT); 
  pinMode(DOWN_BUTTON, INPUT); 
  
  lcd.init();   // initializing the LCD
  lcd.backlight(); // Enable or Turn On the backlight 
  lcd.createChar(1, down_arrow);
  
  if(!connectToWifi()){
    Serial.println(F("Fail to connect. Wrong password? Reset micro controller."));
    resetFunc();
  }
  configureTime();
}

int timezone = 1 * 3600; //GMT +1
int dst = 0; //Daylight saving
void configureTime(){
  configTime(timezone, dst, "pool.ntp.org","time.nist.gov");
  Serial.println(F("Waiting for Internet time"));
  while(!time(nullptr)){
     Serial.print(F("*"));
     delay(1000);
  }
  Serial.println(F("Time response....OK"));
}

bool connectToWifi(){
  Serial.print(F("Connecting to "));
  Serial.println(WIFI_SSID);
  lcd.setCursor(0, 0);
  lcd.print(F("Connecting WiFi "));
  WiFi.mode(WIFI_STA);
  WiFi.begin(WIFI_SSID, WIFI_PWD);
  lcd.setCursor(0,1);
  int count = 0;
  while (WiFi.status() != WL_CONNECTED) {
    delay(500);
    lcd.print(".");
    Serial.print(".");
    count++;
    if(count>15){
      return false;
    }
  }
  lcd.clear();
  Serial.println("");
  lcd.print(F("WiFi connected"));
  Serial.println(F("WiFi connected"));
  Serial.println(F("IP address: "));
  Serial.println(WiFi.localIP()); 
  return true;
}

enum ScreenType {
  FAVOURITE,
  PASSING_TIME
};


class AppState {
  public:
    int upButtonState = 0;
    int selectButtonState = 0;
    int downButtonState = 0;
    ScreenType screen = FAVOURITE;
    String stopIdToFetch;
    int position = 0;
    int previousPosition = 0;
    bool reloadFavourites = true;
    String line1;
    String line2;
};
AppState appState;

void loop() {
  switch(appState.screen) {
    case FAVOURITE:
      handleScreenFavourite();
      break;
    case PASSING_TIME:
      handleScreenPassingTime();
      break;
    default:
      appState.screen = FAVOURITE;
  }
}

void handleScreenFavourite(){
  appState.upButtonState=digitalRead(UP_BUTTON);
  appState.selectButtonState=digitalRead(SELECT_BUTTON);
  appState.downButtonState=digitalRead(DOWN_BUTTON);
  if(appState.selectButtonState == HIGH || appState.upButtonState == HIGH || appState.downButtonState == HIGH){
    if(DEBUG){
      Serial.print(F("Button pushed: "));
      Serial.print(F("selectButtonState: "));Serial.print(appState.selectButtonState);
      Serial.print(F(" upButtonState:"));Serial.print(appState.upButtonState);
      Serial.print(F(" downButtonState"));Serial.println(appState.downButtonState);
    }
    if(appState.selectButtonState == HIGH){
      appState.screen = PASSING_TIME;
      appState.stopIdToFetch = favourites[appState.position].stopId;
      Serial.println(F("Switch to Screen PASSING TIME"));
      lcd.clear();
    } else if(appState.upButtonState == HIGH){
      if(appState.position>0){      
        appState.previousPosition = appState.position;
        appState.position = appState.position-1;
      }else{
        endOfRecord(UP, 2);
      }
    } else if(appState.downButtonState == HIGH){
      if(appState.position+1 < (sizeof(favourites)/sizeof(Favourite))){
        appState.previousPosition = appState.position;
        appState.position = appState.position+1;
      }else{
        endOfRecord(DOWN, 2);
      }
    }
    debouncePushButtons();
  }
  //Display favourites
  if(appState.position != appState.previousPosition || appState.reloadFavourites ){
    bool clearLcd = false;
    int arrowPosition = 0;
    if(DEBUG){
      Serial.print(F("Position changed: Position="));
      Serial.print(appState.position);
      Serial.print(F(" Previous pos:"));
      Serial.println(appState.previousPosition);
    }
    int modulo = appState.position % 2;
    if(appState.position > appState.previousPosition || (appState.reloadFavourites && modulo==0)){ //Going down
      if(!appState.reloadFavourites)Serial.println(F("Going down"));
      if(modulo == 1){
        arrowPosition = 1;
      }else{
        clearLcd = true;  
        arrowPosition = 0;
        appState.line1 = favourites[appState.position].label;
        if(appState.position+1 < (sizeof(favourites)/sizeof(Favourite))){
          appState.line2 = favourites[appState.position+1].label;
        }else{
          appState.line2 = "----------------";
        }
      }    
    }else{ //Going up
      if(!appState.reloadFavourites)Serial.println(F("Going up"));
      if(modulo == 1){
        clearLcd = true;
        arrowPosition = 1;
        appState.line1 = favourites[appState.position-1].label;
        appState.line2 = favourites[appState.position].label;
      }else{
        arrowPosition = 0;
      }  
    }
    appState.reloadFavourites = false;
    if(clearLcd){
      Serial.println(F("Refresh favourites screen"));
      lcd.clear();  
      clearLcd = false;
      //Display lines
      lcd.setCursor(2,0);
      lcd.print(appState.line1);
      lcd.setCursor(2,1);
      lcd.print(appState.line2);
    }
    //Display arrow
    lcd.setCursor(0,arrowPosition);
    lcd.print((char)126);
    lcd.setCursor(0,arrowPosition ? 0 : 1);
    lcd.print(" ");
    appState.previousPosition = appState.position;
  }
}

class PassingTimeState{
   public:
    unsigned long lastUpdate = 0;
    int passingTimePage = 0;
    PassingTimeResponse* passingTimeResponse;
};
PassingTimeState passingTimeState;
void handleScreenPassingTime(){  
  unsigned long elapsedTimeSinceLastUpdate = millis() - passingTimeState.lastUpdate;
  if(elapsedTimeSinceLastUpdate < REFRESH_RATE_SEC * 1000 ){
    appState.upButtonState=digitalRead(UP_BUTTON);
    appState.selectButtonState=digitalRead(SELECT_BUTTON);
    appState.downButtonState=digitalRead(DOWN_BUTTON);
    if(appState.selectButtonState == HIGH || appState.upButtonState == HIGH || appState.downButtonState == HIGH){
      if(appState.selectButtonState == HIGH){
        appState.screen = FAVOURITE;
        appState.reloadFavourites = true;
        passingTimeState.lastUpdate = 0;
        Serial.println(F("Switch to Screen FAVOURITE"));
      }else if(appState.downButtonState == HIGH){
        if(passingTimeState.passingTimePage < (passingTimeState.passingTimeResponse->numberOfResponses/2 + passingTimeState.passingTimeResponse->numberOfResponses%2)){
          passingTimeState.passingTimePage = passingTimeState.passingTimePage+1;
          displayPassingTimeOnLcd(passingTimeState.passingTimeResponse, passingTimeState.passingTimePage); 
        }else{
          endOfRecord(DOWN, 0);
        }
      }else if(appState.upButtonState == HIGH){
        if(passingTimeState.passingTimePage > 1){
          passingTimeState.passingTimePage = passingTimeState.passingTimePage-1;
          displayPassingTimeOnLcd(passingTimeState.passingTimeResponse, passingTimeState.passingTimePage); 
        }else{
          endOfRecord(UP, 0);
        }
      }
      debouncePushButtons();
    }
  }else{
    lcd.setCursor(0,0);
    lcd.print(F("Loading..."));
    passingTimeState.passingTimeResponse = getPassingTime(appState.stopIdToFetch);
    if( passingTimeState.passingTimeResponse != 0 ){
      if(DEBUG){
        Serial.println(F("Response:"));
        unsigned long numberOfSecSinceBeginOfDay = getNumberOfSecSinceBeginOfDay();
        for(int k =0; k<passingTimeState.passingTimeResponse->numberOfResponses ; k++){
          Serial.println(formatPassingTimeForLcd(passingTimeState.passingTimeResponse->passingTimes[k],numberOfSecSinceBeginOfDay) + " - " +passingTimeState.passingTimeResponse->passingTimes[k]->getRawExpectedTime());
        }
        Serial.println(F("---------------"));
      }
      passingTimeState.passingTimePage = 1;
      displayPassingTimeOnLcd(passingTimeState.passingTimeResponse, passingTimeState.passingTimePage); 
    }else{
      lcd.clear();
      lcd.print("Error");
    }
    passingTimeState.lastUpdate = millis();
  }
}

void debouncePushButtons(){
  while(appState.selectButtonState == HIGH || appState.upButtonState == HIGH || appState.downButtonState == HIGH){
    appState.upButtonState=digitalRead(UP_BUTTON);
    appState.selectButtonState=digitalRead(SELECT_BUTTON);
    appState.downButtonState=digitalRead(DOWN_BUTTON);
  }
}

/** Display a small message for the user to tell him that he reached the top/bottom of the list*/
void endOfRecord(UP_DOWN direction, int leftPosition){
  if(direction == DOWN){
    lcd.setCursor(leftPosition,1);
    lcd.print(F("<<Bottom>>"));
    delay(1000);
    lcd.setCursor(leftPosition,1);
    lcd.print(appState.line2);
  }else{
    lcd.setCursor(leftPosition,0);
    lcd.print(F("<< Top >>"));
    delay(1000);
    lcd.setCursor(leftPosition,0);
    lcd.print(appState.line1);    
  }
}

unsigned long getNumberOfSecSinceBeginOfDay(){
  time_t now = time(nullptr);
  struct tm* p_tm = localtime(&now);
  while(p_tm->tm_year < 100){
    Serial.print("Current year: ");
    Serial.print(p_tm->tm_year);
    Serial.println(" [ERROR] Current date is not fully initialized! Delay 200ms");
    delay(200);
    now = time(nullptr);
    p_tm = localtime(&now);
  }
  if(DEBUG){
    Serial.print(F("Current time:"));
    Serial.print(p_tm->tm_hour);
    Serial.print(":");
    Serial.print(p_tm->tm_min);
    Serial.print(":");
    Serial.println(p_tm->tm_sec);
  }
  return p_tm->tm_hour *3600 + p_tm->tm_min *60 + p_tm->tm_sec;
}

String formatPassingTimeForLcd(PassingTime *passingTime, unsigned long secSinceBeginOfDay){
  long remainingTime = passingTime->getRemainingTime(secSinceBeginOfDay);
  String remainingTimeStr = String(remainingTime);
  if(remainingTime == 0){
    remainingTimeStr = DOWN_ARROW + DOWN_ARROW;
  }else if(remainingTime < 10){
    remainingTimeStr = " " + remainingTimeStr;
  }else if(remainingTime > 90){
    remainingTimeStr = "--";
  }
  
  return (passingTime->getLine() + "  ").substring(0,3) + (passingTime->getDestination() + "     ").substring(0, 10) + " " + remainingTimeStr;
}


void displayPassingTimeOnLcd(PassingTimeResponse* passingTimeResponse, int page){
  lcd.clear();
  unsigned long numberOfSecSinceBeginOfDay = getNumberOfSecSinceBeginOfDay();
  appState.line1 = formatPassingTimeForLcd(passingTimeResponse->passingTimes[(page-1)*2],numberOfSecSinceBeginOfDay);
  if((page-1)*2 + 1 < passingTimeResponse->numberOfResponses){
    appState.line2 = formatPassingTimeForLcd(passingTimeResponse->passingTimes[(page-1)*2 + 1],numberOfSecSinceBeginOfDay);
  }else{
    appState.line2 = "----------------";
  }
  lcd.print(appState.line1);
  lcd.setCursor(0,1);
  lcd.print(appState.line2);
}

// code stored in the sketch: StibIotHttpClient2.ino
/*
    Small device to retrieve the passing time of the STIB-MIVB public transport at given stops.
    These stops are hardcoded in the code as favourites. 
    The app consists in 2 screen. 
    - The selection of the line from the favourite list.
    - Displaying the time at station
    The user has 3 push buttons. 
    2 for going up/down. 1 for selecting a favourite/going back to favourites page

    Components:
    - NodeMcu
    - LCD-I2C
    - 3 push buttons
    - 3 10K Ohm resistors

    Librairies:
    - ArduinoJson: https://arduinojson.org/
    - ArduinoSort: https://github.com/emilv/ArduinoSort
    - LiquidCrystal I2C: https://github.com/johnrickman/LiquidCrystal_I2C

    Resources:
    - Configure NodeMcu: https://www.youtube.com/watch?v=p06NNRq5NTU

    TODO:
    - Regenerate token
    - Wake up on push
    - led indicator (loading)
    - Get remaining time instead of expected time arrival
    - Auto refresh every 15sec
    - 3D print case
*/
#define DEBUG true
#include "PassingTime.h"
#include "Favourite.h"
//Configure STASSID, STAPSK, API_TOKEN and favourites
#include "config.h"
const char* ssid = STASSID;
const char* password = STAPSK;
const char* token = API_TOKEN;

/** Librairies */
#include <ESP8266WiFi.h>
#include <ESP8266HTTPClient.h>
#include <WiFiClientSecureBearSSL.h>
#include "ArduinoJson.h"
#include <ArduinoSort.h>
#include <Wire.h>  // This library is already built in to the Arduino IDE
#include <LiquidCrystal_I2C.h> //This library you can add via Include Library > Manage Library > 

LiquidCrystal_I2C lcd(0x27, 16, 2);

const String APP_NAME = "Stib IOT - " __FILE__;
const String APP_VERSION = "v0.1-" __DATE__ " " __TIME__;

/** STIB-MIVB endpoint configuration */
const String host = "https://opendata-api.stib-mivb.be";
const int httpsPort = 443;
const String endPointToken = "/token";
const String endPointPassingTime = host + "/OperationMonitoring/3.0/PassingTimeByPoint";
// Use web browser to view and copy
// SHA1 fingerprint of the certificate
const char fingerprint[] PROGMEM = "5f 88 a4 69 77 f0 69 00 5d 6f 71 19 3d e2 2e 20 44 48 f0 b3";

DynamicJsonBuffer jsonBuffer(100);
PassingTime *passingTimes[10];
const char * headerKeys[] = {"date"};
const size_t numberOfHeaders = 1;

enum UP_DOWN{
  UP,
  DOWN
};

#define UP_BUTTON D4
#define SELECT_BUTTON D5
#define DOWN_BUTTON D6

void setup() {
  Serial.begin(115200);
  Serial.println();
  Serial.println(APP_NAME);
  Serial.println(APP_VERSION);
  if(DEBUG)Serial.println(F("Debug mode"));
  
  
  pinMode(UP_BUTTON, INPUT);
  pinMode(SELECT_BUTTON, INPUT); 
  pinMode(DOWN_BUTTON, INPUT); 
  
  lcd.init();   // initializing the LCD
  lcd.backlight(); // Enable or Turn On the backlight 

  if(!connectToWifi()){
    Serial.println("Fail to connect. Reset micro controller.");
    setup();
  }
}

bool connectToWifi(){
  Serial.print(F("Connecting to "));
  Serial.println(ssid);
  lcd.print(F("Connecting WiFi "));
  WiFi.mode(WIFI_STA);
  WiFi.begin(ssid, password);
  lcd.setCursor(0,1);
  int count = 0;
  while (WiFi.status() != WL_CONNECTED) {
    delay(500);
    lcd.print(".");
    Serial.print(".");
    count++;
    if(count>10){
      return false;
    }
  }
  lcd.clear();
  Serial.println("");
  lcd.print(F("WiFi connected"));
  Serial.println(F("WiFi connected"));
  Serial.println(F("IP address: "));
  Serial.println(WiFi.localIP()); 
  return true;
}

PassingTimeResponse* getPassingTime(String stopId){
  String url = endPointPassingTime + "/" + stopId;
  Serial.print(F("[HTTPS] begin: "));
  Serial.println(url);
  
  std::unique_ptr<BearSSL::WiFiClientSecure>client(new BearSSL::WiFiClientSecure);
  client->setFingerprint(fingerprint);
  HTTPClient http;
  lcd.clear();
  lcd.print(F("Get passing time"));
  if (http.begin(*client, url)) {  // HTTP
      http.addHeader(F("Accept"), F("application/json"));
      http.addHeader(F("Authorization"), token);
      Serial.println(F("[HTTPS] GET..."));
      http.collectHeaders(headerKeys, numberOfHeaders);
      // start connection and send HTTP header
      int httpCode = http.GET();
      PassingTimeResponse * passingTimeResponse;
      if (httpCode > 0) {
        // HTTP header has been send and Server response header has been handled
        Serial.print(F("[HTTPS] GET... code:"));
        Serial.println(httpCode);
        
        // file found at server
        if (httpCode == HTTP_CODE_OK || httpCode == HTTP_CODE_MOVED_PERMANENTLY) {
          String payload = http.getString();
          int j = 0;
          Serial.println(http.header(j));
          JsonObject& root = jsonBuffer.parseObject(payload);
          if(!root.success()){
            Serial.println(F("Fail to parse object"));  
            return 0;
          }
          JsonArray& passingTimesArr = root[F("points")][0][F("passingTimes")];
          if(!passingTimesArr.success()){
            Serial.println(F("Fail to parse passingTimes"));  
            return 0;
          }
          passingTimeResponse = getPassingTimeResponse(passingTimesArr);

          if(DEBUG){
            Serial.println(F("Response:"));
            for(int k =0; k<passingTimeResponse->numberOfResponses ; k++){
              Serial.println(passingTimeResponse->passingTimes[k]->getDisplay());
            }
            Serial.println(F("---------------"));
          }
        }
      } else {
        Serial.print(F("[HTTPS] GET... failed, error: "));
        Serial.println(http.errorToString(httpCode));
      }

      http.end();
      return passingTimeResponse;
  } else {
    Serial.println(F("[HTTPS] Unable to connect"));
  }
  return 0;
}

PassingTimeResponse* getPassingTimeResponse(JsonArray& passingTimesArr){
  int i = 0;
  static PassingTime *passingTimes[10];
  for (JsonObject& val : passingTimesArr){
    passingTimes[i] = new PassingTime(val[F("lineId")].as<String>(), val[F("destination")][F("fr")].as<String>(), val[F("expectedArrivalTime")].as<String>());
    Serial.println(passingTimes[i]->getDisplay());
    i++;
  }
  sortArray(passingTimes, i, sortPassingTimes);
  
  return new PassingTimeResponse(passingTimes, i);
}


bool sortPassingTimes(PassingTime *a, PassingTime *b){
  return a->getRemainingTime() > b->getRemainingTime();
}
int upButtonState = 0;
int selectButtonState = 0;
int downButtonState = 0;
String stopIdToFetch;

enum ScreenType {
  FAVOURITE,
  PASSING_TIME
};

ScreenType screen = FAVOURITE;

void loop() {
  switch(screen) {
    case FAVOURITE:
      handleScreenFavourite();
      break;
    case PASSING_TIME:
      handleScreenPassingTime();
      break;
    default:
      screen = FAVOURITE;
  }
  //delay(500);
}

int position = 0;
int previousPosition = 0;
bool reloadFavourites = true;
String line1;
String line2;
bool clearLcd = true;
int arrowPosition = 0;
void handleScreenFavourite(){
  upButtonState=digitalRead(UP_BUTTON);
  selectButtonState=digitalRead(SELECT_BUTTON);
  downButtonState=digitalRead(DOWN_BUTTON);
  if(selectButtonState == HIGH || upButtonState == HIGH || downButtonState == HIGH){
    if(DEBUG){
      Serial.print(F("Button pushed: "));
      Serial.print(F("selectButtonState: "));Serial.print(selectButtonState);
      Serial.print(F(" upButtonState:"));Serial.print(upButtonState);
      Serial.print(F(" downButtonState"));Serial.println(downButtonState);
    }
    if(selectButtonState == HIGH){
      screen = PASSING_TIME;
      stopIdToFetch = favourites[position].stopId;
      Serial.println(F("Switch to Screen PASSING TIME"));
    } else if(upButtonState == HIGH){
      if(position>0){      
        previousPosition = position;
        position = position-1;
      }else{
        endOfRecord(UP, 2);
      }
    } else if(downButtonState == HIGH){
      if(position+1 < (sizeof(favourites)/sizeof(Favourite))){
        previousPosition = position;
        position = position+1;
      }else{
        endOfRecord(DOWN, 2);
      }
    }
    debouncePushButtons();
  }
  //Display favourites
  if(position != previousPosition || reloadFavourites ){
    if(DEBUG){
      Serial.print(F("Position changed: Position="));
      Serial.print(position);
      Serial.print(F(" Previous pos:"));
      Serial.println(previousPosition);
    }
    int modulo = position % 2;
    if(position > previousPosition || (reloadFavourites && modulo==0)){ //Going down
      if(!reloadFavourites)Serial.println(F("Going down"));
      if(modulo == 1){
        arrowPosition = 1;
      }else{
        clearLcd = true;  
        arrowPosition = 0;
        line1 = favourites[position].label;
        if(position+1 < (sizeof(favourites)/sizeof(Favourite))){
          line2 = favourites[position+1].label;
        }else{
          line2 = "----------------";
        }
      }    
    }else{ //Going up
      if(!reloadFavourites)Serial.println(F("Going up"));
      if(modulo == 1){
        clearLcd = true;
        arrowPosition = 1;
        line1 = favourites[position-1].label;
        line2 = favourites[position].label;
      }else{
        arrowPosition = 0;
      }  
    }
    reloadFavourites = false;
    if(clearLcd){
      Serial.println(F("Refresh favourites screen"));
      lcd.clear();  
      clearLcd = false;
      //Display lines
      lcd.setCursor(2,0);
      lcd.print(line1);
      lcd.setCursor(2,1);
      lcd.print(line2);
    }
    //Display arrow
    lcd.setCursor(0,arrowPosition);
    lcd.print(">");
    lcd.setCursor(0,arrowPosition ? 0 : 1);
    lcd.print(" ");
    previousPosition = position;
  }
}
bool passingTimeLoaded = false;
int passingTimePage = 0;
PassingTimeResponse* passingTimeResponse;
void handleScreenPassingTime(){  
  if(passingTimeLoaded){
    upButtonState=digitalRead(UP_BUTTON);
    selectButtonState=digitalRead(SELECT_BUTTON);
    downButtonState=digitalRead(DOWN_BUTTON);
    if(selectButtonState == HIGH || upButtonState == HIGH || downButtonState == HIGH){
      if(selectButtonState == HIGH){
        screen = FAVOURITE;
        reloadFavourites = true;
        passingTimeLoaded = false;
        Serial.println(F("Switch to Screen FAVOURITE"));
      }else if(downButtonState == HIGH){
        if(passingTimePage < (passingTimeResponse->numberOfResponses/2 + passingTimeResponse->numberOfResponses%2)){
          passingTimePage = passingTimePage+1;
          displayPassingTimeOnLcd(passingTimeResponse, passingTimePage); 
        }else{
          endOfRecord(DOWN, 0);
        }
      }else if(upButtonState == HIGH){
        if(passingTimePage > 1){
          passingTimePage = passingTimePage-1;
          displayPassingTimeOnLcd(passingTimeResponse, passingTimePage); 
        }else{
          endOfRecord(UP, 0);
        }
      }
      debouncePushButtons();
    }
  }else{
    passingTimeResponse = getPassingTime(stopIdToFetch);
    if( passingTimeResponse != 0 ){
      passingTimePage = 1;
      displayPassingTimeOnLcd(passingTimeResponse, passingTimePage); 
    }else{
      lcd.clear();
      lcd.print("Error");
    }
    passingTimeLoaded = true;
  }
}

void debouncePushButtons(){
  while(selectButtonState == HIGH || upButtonState == HIGH || downButtonState == HIGH){
    upButtonState=digitalRead(UP_BUTTON);
    selectButtonState=digitalRead(SELECT_BUTTON);
    downButtonState=digitalRead(DOWN_BUTTON);
  }
}

/** Display a small message for the user to tell him that he reached the top/bottom of the list*/
void endOfRecord(UP_DOWN direction, int leftPosition){
  if(direction == DOWN){
    lcd.setCursor(leftPosition,1);
    lcd.print(F("<<Bottom>>"));
    delay(1000);
    lcd.setCursor(leftPosition,1);
    lcd.print(line2);
  }else{
    lcd.setCursor(leftPosition,0);
    lcd.print(F("<< Top >>"));
    delay(1000);
    lcd.setCursor(leftPosition,0);
    lcd.print(line1);    
  }
}

void displayPassingTimeOnLcd(PassingTimeResponse* passingTimeResponse, int page){
  lcd.clear();
  line1 = passingTimeResponse->passingTimes[(page-1)*2]->getDisplay();
  if((page-1)*2 + 1 < passingTimeResponse->numberOfResponses){
    line2 = passingTimeResponse->passingTimes[(page-1)*2 + 1]->getDisplay();
  }else{
    line2 = "----------------";
  }
  lcd.print(line1);
  lcd.setCursor(0,1);
  lcd.print(line2);
}
